# Fritzing sketch mazeSolverUpdated (saved by Fritzing 0.9.3b)
breadboards: 1

parts:
  Teensy1 = Teensy 4.1
  S2 = Taiway 100-SP-X-T1 SPDT Miniature Toggle Switch [part_number=100-SP-X-T1-0-0-B1-M1 package=THT]
  Grove1 = Grove OLED 128x96
  Part3 = Motor Driver 1A Dual TB6612FNG
  M3 = RioRand LM2596
  M4 = RioRand LM2596
  DC_Mot_Enc1 = DC Motor with two-phase hall-encoder [part_number=VT-E-G25A-06-177E]
  DC_Mot_Enc2 = DC Motor with two-phase hall-encoder [part_number=VT-E-G25A-06-177E]
  Part4 = VL530X Time of Flight Distance Sensor [part_number="tonetoys #3317"]
  Componente2 = 9-DOF Absolute Orientation IMU Fusion Breakout - BNO055
  Part5 = VL530X Time of Flight Distance Sensor [part_number="tonetoys #3317"]
  Part6 = VL530X Time of Flight Distance Sensor [part_number="tonetoys #3317"]
  M5 = fc-51 [package=THT]
  M6 = fc-51 [package=THT]
  BAT1 = Battery Holders [package=lipo-1100mAh]
  BAT2 = Battery Holders [package=lipo-1100mAh]
  BAT3 = Battery Holders [package=lipo-1100mAh]
  BAT4 = Battery Holders [package=lipo-1100mAh]
  M7 = fc-51 [package=THT]
  M8 = fc-51 [package=THT]
  TXS0108E_8-Bit_Bi-directional_Level-Shifting_Voltage_Translator1 = TXS0108 [part_number=TXS0108EPW package=TSSOP]  # not connected
  LED1 = RGB LED (com. cathode, rbg) [package="5 mm [THT]"]
  R1 = Resistor [tolerance=±5% resistance=330 package=THT]
  S3 = Round Pushbutton
  S4 = Round Pushbutton
  R2 = Resistor [tolerance=±5% resistance=220 package=THT]
  R3 = Resistor [tolerance=±5% resistance=220 package=THT]

nets:
  N1: Teensy1.GND, Teensy1.GND2#55
  N2: Teensy1.A0/D14, Part3.PWMA
  N3: Teensy1.A1/D15, Part3.PWMB
  N4: Teensy1.A2/D16, Part4.SCL, Part5.SCL, Part6.SCL
  N5: Teensy1.A3/D17, Part4.SDA, Part5.SDA, Part6.SDA
  N6: Teensy1.A4/D18, Componente2.SDA_5V
  N7: Teensy1.A5/D19, Componente2.SCL_5V
  N8: Teensy1.A6/D20, Part3.STBY
  N9: Teensy1.A7/D21, Part4.XSHUT
  N10: Teensy1.A8/D22, Part6.XSHUT
  N11: Teensy1.A9/D23, Part5.XSHUT
  N12: Teensy1.3V3_LOW, Grove1.VCC, DC_Mot_Enc1.pin2, DC_Mot_Enc2.pin2
  GND: Teensy1.GND2#31, Grove1.GND, Part3.GND, M3.Pin_2, M3.Pin_4, M4.Pin_2, M4.Pin_4, DC_Mot_Enc1.pin5, DC_Mot_Enc2.pin5, Part4.GND, Componente2.GND, Part5.GND, Part6.GND, M5.pin2, M6.pin2, BAT4.-, M7.pin2, M8.pin2, R1.Pin_0, R2.Pin_0, R3.Pin_0
  VCC: Teensy1.Vin, M3.Pin_3, Part4.VCC, Componente2.5.0V, Part5.VCC, Part6.VCC, M5.pin3, M6.pin3, M7.pin3, M8.pin3
  N13: Teensy1.A10/D24, Grove1.SCL
  N14: Teensy1.A11/D25, Grove1.SDA
  N15: Teensy1.A13/D27, LED1.green_anode
  N16: Teensy1.D28, LED1.blue_anode
  N17: Teensy1.D29, LED1.red_anode
  N18: Teensy1.D30, S3.leg0
  N19: Teensy1.D31, S4.leg0
  N20: Teensy1.D33, DC_Mot_Enc1.pin3
  N21: Teensy1.D34, DC_Mot_Enc1.pin4
  N22: Teensy1.D36, DC_Mot_Enc2.pin4
  N23: Teensy1.D37, DC_Mot_Enc2.pin3
  N24: Teensy1.A14/D38, Part3.AIN2
  N25: Teensy1.A15/D39, Part3.AIN1
  N26: Teensy1.A16/D40, Part3.BIN2
  N27: Teensy1.A17/D41, Part3.BIN1
  N28: S2.L1, BAT2.+
  N29: S2.L2, Part3.VM, M3.Pin_1, M4.Pin_1
  N30: Part3.B01, DC_Mot_Enc2.pin1
  N31: Part3.B02, DC_Mot_Enc2.pin6
  N32: Part3.A02, DC_Mot_Enc1.pin1
  N33: Part3.A01, DC_Mot_Enc1.pin6
  N34: Part3.VCC, M4.Pin_3
  N35: BAT1.+, BAT3.-
  N36: BAT1.-, BAT4.+
  N37: BAT2.-, BAT3.+

custom parts:
  Teensy 4.1: The Teensy is a complete USB-based microcontoller development system, in a very small footprint, capable of implementing many types of projects. All programming is done via the USB port. No special programmer is needed, only a standard micro-USB cable and a PC or Macintosh with a USB port.
  VL530X Time of Flight Distance Sensor: TOF
  9-DOF Absolute Orientation IMU Fusion Breakout - BNO055: A MEMS accelerometer, magnetometer and gyroscope on a single die with a high speed ARM Cortex-M0 based processor to digest all the sensor data, abstract the sensor fusion and real time requirements away, and spit out data you can use in quaternions, Euler angles or vectors.
  TXS0108: This 8-bit non-inverting translator uses two separate configurable power-supply rails. The A port tracks the VCCA pin supply voltage. The VCCA pin accepts any supply voltage between 1.2 V and 3.6 V. The B port tracks the VCCB pin supply voltage. The VCCB pin accepts any supply voltage between 1.65 V and 5.5 V. Two input supply pins allows for low Voltage bidirectional translation between any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
